# Fritzing sketch NFC_Door (saved by Fritzing 0.9.4)
circuit board: 8.46667cm x 5.64444cm
breadboards: 1

parts:
  U1 = ESP32-38PinWide [part_number=ESP32-38PinWide]
  U2 = RFID RC522 SIP - 8 pins [chip_label="RFID RC522" package="SIP (Single Inline) [THT]"]
  U3 = WS2812 RGB LED strip
  Keypad4x1 = Keypad Membran 4x4
  U4 = WS2812 RGB LED strip
  M1 = RioRand LM2596

nets:
  N1: U1.3.3, U2.VCC
  N2: U1.GPIO26, U2.RST
  N3: U1.GPIO27, U2.NSS
  N4: U1.GPIO14, U2.SCK
  N5: U1.GPIO12, U2.MISO
  GND: U1.GND, U2.GND, U3.GND#0, M1.Pin_4
  N6: U1.GPIO13, U2.MOSI
  N7: U1.VIN, U3.VCC#1, M1.Pin_3
  N8: U1.GPIO15, Keypad4x1.Pin8
  N9: U1.GPIO2, Keypad4x1.Pin7
  N10: U1.GPIO0, Keypad4x1.Pin6
  N11: U1.GPIO4, Keypad4x1.Pin5
  N12: U1.GPIO16, Keypad4x1.Pin4
  N13: U1.GPIO17, Keypad4x1.Pin3
  N14: U1.GPIO5, Keypad4x1.Pin2
  N15: U1.GPIO18, Keypad4x1.Pin1
  N16: U1.GPIO21, U3.DIN
  N17: U3.GND#4, U4.GND
  N18: U3.VCC#5, U4.VCC
  N19: U3.DOUT, U4.DIN

custom parts:
  ESP32-38PinWide: Generic 38-Pin ESP32 with wide format (only access to one side of pins on a breadboard) based on Stephen Lilley's HiLetgo ESP-WROOM-32 ESP32 ESP-32S Development Board.
  RFID RC522 SIP - 8 pins: A SIP stand-in part for RFID RC522 . With 8 pins on a 300 mil single inline package (SIP) footprint.
  WS2812 RGB LED strip: WS2812 strip
  Keypad Membran 4x4: Membrane Keypad 4x4 Matrix
